# Fritzing sketch circuit_scheme (saved by Fritzing 0.9.3b)
breadboards: 6

parts:
  Part1 = Arduino Uno (Rev3)
  U1 = 74HC595 [package="DIP16 [THT]"]
  U2 = 74HC595 [package="DIP16 [THT]"]  # not connected
  U3 = 74HC595 [package="DIP16 [THT]"]  # not connected
  U4 = 74HC595 [package="DIP16 [THT]"]  # not connected
  IC1 = DS1307 [package=THT]

nets:
  N1: Part1.A4/SDA, IC1.SDA_-_I2C_Data
  N2: Part1.A5/SCL, IC1.SCL_-_I2C_Clock
  N3: Part1.D8, U1.ST_CP
  N4: Part1.D11_PWM/MOSI, U1.DS
  N5: Part1.D12/MISO, U1.SH_CP
  5V: Part1.5V, U1.MR, U1.VCC, IC1.+V
  GND: Part1.GND, U1.GND, U1.OE, IC1.0V

notes:
  Note 1: The actual RTC element used was DS1338. It was wired the same way - same pins on the element connected to the same pins on the Arduino
